# Fritzing sketch circuitry (saved by Fritzing 0.9.3b)
breadboards: 1

parts:
  Part1 = Arduino Uno (Rev3)
  Q1 = NPN-Transistor [package="TO92 [THT]"]
  Q2 = NPN-Transistor [package="TO92 [THT]"]
  Q3 = NPN-Transistor [package="TO92 [THT]"]
  J1 = Camdenboss CTB0158-4 [part_number=CTB0158-4 package=THT]
  R2 = Resistor [tolerance=±5% resistance=330 package=THT]
  R3 = Resistor [tolerance=±5% resistance=330 package=THT]
  R4 = Resistor [tolerance=±5% resistance=330 package=THT]
  RGB_Strip_LED3 = RGB Strip LED
  RGB_Strip_LED4 = RGB Strip LED  # not connected
  U2 = NodeMCU V3.0
  R5 = Resistor [tolerance=±5% resistance=330 package=THT]

nets:
  N1: Part1.D10_PWM/SS, U2.D5
  N2: Part1.D11_PWM/MOSI, U2.D6
  GND: Part1.GND, U2.GND, R5.Pin_1
  N3: Part1.D3_PWM, R2.Pin_0
  N4: Part1.D4, R3.Pin_0
  N5: Part1.D5_PWM, R4.Pin_0
  VIN: Part1.VIN, U2.Vin
  N6: Q1.E, RGB_Strip_LED3.Blue_Connect
  N7: Q1.B, R4.Pin_1
  N8: Q1.C, J1.terminal_1, R5.Pin_0
  N9: Q2.E, RGB_Strip_LED3.Green_Connect
  N10: Q2.B, R3.Pin_1
  N11: Q2.C, J1.terminal_3
  N12: Q3.E, RGB_Strip_LED3.Red_Connect
  N13: Q3.B, R2.Pin_1
  N14: Q3.C, J1.terminal_2
  N15: J1.terminal_4, RGB_Strip_LED3.Common_Connect

custom parts:
  RGB Strip LED: A tri-color Strip LED with red, green and blue. Based on LED SMD 5050 RGB Pin order: common cathode - green - red - blue
  NodeMCU V3.0: ESP8266 based NodeMCU
